# Fritzing sketch Untitled Sketch (saved by Fritzing 0.9.3b)
circuit board: 5.19752cm x 5.98473cm
breadboards: 1

parts:
  R1 = Resistor [tolerance=±5% resistance=1M package=THT]
  R2 = Resistor [tolerance=±5% resistance=180k package=THT]
  R3 = Resistor [tolerance=±5% resistance=370k package=THT]
  R4 = Resistor [tolerance=±5% resistance=100k package=THT]
  S1 = Pushbutton [package="[THT]"]
  U1 = atmega328 [package=dip]
  U3 = Voltage Regulator [package=to220-adj]
  R6 = Resistor [tolerance=±5% resistance=100k package=THT]
  R7 = Resistor [tolerance=±5% resistance=470k package=THT]
  U5 = RF-LINK_TX [package=rf-link_tx]
  Q1 = NPN-Transistor [package="TO92 [THT]"]
  R5 = Temperature Sensor (Thermistor) [thermistor_type=PTC package=THT]
  R8 = Resistor [tolerance=±5% resistance=2.75k package=THT]
  VCC1 = Battery block 9V

nets:
  N1: R1.Pin_0, U1.A0, R5.pin_0
  GND: R1.Pin_1, R2.Pin_0, S1.Pin_3, S1.Pin_4, U1.GND, R6.Pin_1, U5.GND, VCC1.-
  N2: R2.Pin_1, R3.Pin_0, U3.ADJ
  N3: R3.Pin_1, R4.Pin_1, U1.VCC, U1.AVCC, U3.OUT, R5.pin_1
  N4: R4.Pin_0, S1.Pin_1, S1.Pin_2, U1.RESET
  N5: U1.D12, U5.DATA
  N6: U1.D13, R8.Pin_1
  N7: U1.A1, R6.Pin_0, R7.Pin_1
  N8: U3.IN, R7.Pin_0, Q1.C, VCC1.+
  N9: U5.+5V, Q1.E
  N10: Q1.B, R8.Pin_0
